# Fritzing sketch circut digram (saved by Fritzing 0.9.3b)
breadboards: 1

parts:
  RE1 = KY-040 Rotary encoder [package=THT]
  U1 = atmega328 [package=dip]
  S1 = Pushbutton [package="[THT]"]
  S2 = Pushbutton [package="[THT]"]
  U2 = LIPO-110mAh [package=lipo-110]
  Part1 = LCD1602-I2C
  TP1 = TP4056 [chip_label=TP4056 package="DIP (Dual Inline) [THT]"]
  Boost_Convertor1 = Boost Convertor [part_number=XL6009E1 package=THT]
  C1 = Ceramic Capacitor [capacitance=22pF package="200 mil [THT, multilayer]"]
  R1 = Resistor [tolerance=±5% resistance=10k package=THT]
  XTAL1 = Crystal [frequency="16 Mhz" package=THT]
  C2 = Ceramic Capacitor [capacitance=22pF package="100 mil [THT, multilayer]"]
  R2 = Resistor [tolerance=±5% resistance=10k package=THT]
  R3 = Resistor [tolerance=±5% resistance=10k package=THT]

nets:
  GND: RE1.GND, U1.GND, Part1.GND, Boost_Convertor1.Negative_Output, C1.1, C2.0, R2.Pin_1, R3.Pin_1
  VCC: RE1.Vcc, U1.VCC, U1.AVCC, U1.AREF, S1.Pin_3, S1.Pin_4, S2.Pin_3, S2.Pin_4, Part1.VCC, Boost_Convertor1.Positive_Output, R1.Pin_0
  N1: RE1.DT, U1.D3_(PWM)
  N2: RE1.CLK, U1.D2
  N3: U1.RESET, R1.Pin_1
  N4: U1.XLAT1, XTAL1.pin_0, C2.1
  N5: U1.XLAT2, C1.0, XTAL1.pin_1
  N6: U1.D5_(PWM), S1.Pin_1, S1.Pin_2, R2.Pin_0
  N7: U1.D7, S2.Pin_1, S2.Pin_2, R3.Pin_0
  N8: U1.A4, Part1.SDA
  N9: U1.A5, Part1.SCL
  N10: U2.+, TP1.pin4
  N11: U2.-, TP1.pin5
  N12: TP1.pin3, Boost_Convertor1.Positive_Input
  N13: TP1.pin6, Boost_Convertor1.Negative_Input

custom parts:
  KY-040 Rotary encoder: KY-040 Rotary Encoder with switch on breakout borad from AZ Delivery
  LCD1602-I2C: A standard character display, usually with 2x16 characters. Comes in many colors with LCM1602 IIC attached.
  TP4056: A DIP stand-in part for whatever IC you want. With 6 pins on a 300mil dual inline package (DIP) footprint.
  Boost Convertor: DC to DC boost convertor
